# Fritzing sketch EnviroMonitor (saved by Fritzing 0.9.3b)
circuit board: 6cm x 6cm
breadboards: 1

parts:
  DC5 = Camdenboss CTB0158-2 [part_number=CTB0158-2 package=THT]
  HEAT_RELAY = Basic FET N-Channel [package="TO220 [THT]"]
  DC12 = Camdenboss CTB0158-2 [part_number=CTB0158-2 package=THT]
  HEAT = Camdenboss CTB0158-2 [part_number=CTB0158-2 package=THT]
  HEAT_DC_SW = SPST Switch [package=switch-spdt_kit]
  PMS = rounded female pin header, 6 pins [form="♀ (female rounded)"]
  I2C = rounded female pin header, 4 pins [form="♀ (female rounded)"]
  DHT = rounded female pin header, 3 pins [form="♀ (female rounded)"]
  R3 = Resistor [tolerance=±5% resistance=1k package=THT]
  R2 = Resistor [tolerance=±5% resistance=47k package=THT]
  R1 = Resistor [tolerance=±5% resistance=4.7k package=THT]
  DS1 = rounded female pin header, 3 pins [form="♀ (female rounded)"]
  WeMos_D1_Mini1 = WeMos D1 Mini_v2

nets:
  5V: DC5.pin1, HEAT_DC_SW.S, PMS.pin1, DHT.pin1, R3.Pin_0, R1.Pin_1, DS1.pin3, WeMos_D1_Mini1.5V
  GND: DC5.pin2, HEAT_RELAY.source, DC12.pin2, PMS.pin2, I2C.pin2, DHT.pin2, R2.Pin_0, DS1.pin1, WeMos_D1_Mini1.G
  N1: HEAT_RELAY.gate, R2.Pin_1, WeMos_D1_Mini1.D4
  N2: HEAT_RELAY.drain, HEAT.pin2
  12V: DC12.pin1, HEAT_DC_SW.O
  N3: HEAT.pin1, HEAT_DC_SW.P
  N4: PMS.pin3, WeMos_D1_Mini1.D5
  N5: PMS.pin4, WeMos_D1_Mini1.D6
  N6: PMS.pin5, WeMos_D1_Mini1.D7
  N7: PMS.pin6, WeMos_D1_Mini1.D8
  3.3V: I2C.pin1, WeMos_D1_Mini1.3V3
  N8: I2C.pin3, WeMos_D1_Mini1.D2
  N9: I2C.pin4, WeMos_D1_Mini1.D1
  N10: DHT.pin3, R3.Pin_1, WeMos_D1_Mini1.D0
  N11: R1.Pin_0, DS1.pin2, WeMos_D1_Mini1.D3

notes:
  PMS3003 connector (right to left)
  PIN1 - 5VCC
  PIN2 - GND
  PIN3 - SET (D5)
  PIN4 - RXD (connect to TX of Wemos D6)
  PIN5 - TXD (connect to RX of Wemos D7)
  PIN6 - RST (D8)
  I2C bus connector
  PIN1 - 3.3VCC
  PIN2 - GND
  PIN3 - SCL
  PIN4 - SDA
  DC5 - External 5VCC
  DC12 - External 12VCC
  HEAT - Heater connector
  DHT connector
  PIN1 - 5VCC
  PIN2 - GND
  PIN3 - Data
  Enviro
  v1.0
  1
  5V
  GND
  SET
  RX
  TX
  RST
  12V
  3V3
  SDA
  SCL
  Monitor
  DS18B20 connector
  PIN1 - GND
  PIN2 - Data
  PIN3 - 5VCC
  DTA
  +
  -

custom parts:
  WeMos D1 Mini_v2: The D1 mini is a mini wifi board based on ESP-8266EX.
